# Fritzing sketch main (saved by Fritzing 0.9.4)
breadboards: 1

parts:
  YwRobot_Power_Supply1 = YwRobot Breadboard Power Supply [part_number=545043]
  U1 = NodeMCU V3.0
  J1 = Basic Servo

nets:
  N1: YwRobot_Power_Supply1.VCC#5, YwRobot_Power_Supply1.VCC#6, U1.3V3
  N2: YwRobot_Power_Supply1.VCC#9, YwRobot_Power_Supply1.VCC#10, J1.vcc
  N3: YwRobot_Power_Supply1.GND#11, YwRobot_Power_Supply1.GND#12, U1.GND
  N4: YwRobot_Power_Supply1.GND#13, YwRobot_Power_Supply1.GND#14, J1.gnd
  N5: U1.D4, J1.pulse

notes:
  The green wire is connected to the second pin of the servo potentiometer

custom parts:
  YwRobot Breadboard Power Supply: The YwRobot Breadboard Power Supply (MB-V2) has two power rails; they can be 5V or 3V3. Power to the module can be provided through the female USB socket or through the A10 (female) 2.1mm power jack.
  NodeMCU V3.0: NodeMcu V3 Lua WIFI Development Board
